# Fritzing sketch horimetro_lorawan_sch (saved by Fritzing 0.9.3b)
breadboards: 1

parts:
  Heltec_WiFi_LoRa_1 = Heltec WiFi LoRa 32 [part_number=HTIT-WB32LA]
  S1 = Momentary Switch [package=ksa_sealed_tac_switch]
  R1 = Resistor [tolerance=±5% resistance=100k package="2512 [SMD]"]

nets:
  N1: Heltec_WiFi_LoRa_1.pin_15, S1.3, R1.Pin_0
  N2: Heltec_WiFi_LoRa_1.pin_16, Heltec_WiFi_LoRa_1.pin_21, S1.1
  N3: Heltec_WiFi_LoRa_1.pin_17, Heltec_WiFi_LoRa_1.pin_20
  N4: Heltec_WiFi_LoRa_1.pin_18, Heltec_WiFi_LoRa_1.pin_19, Heltec_WiFi_LoRa_1.pin_22, R1.Pin_1

custom parts:
  Heltec WiFi LoRa 32: Heltec WiFi LoRa 32 WiFi LoRa 32 is a classic IoT dev-board designed & produced by Heltec Automation(TM). It’s a highly integrated product based on ESP32 + SX127x, it has Wi-Fi, BLE, LoRa functions, also Li-Po battery management system, 0.96″ OLED are also included. It’s the best choice for smart cities, smart farms, smart home, and IoT makers.
